# Fritzing sketch PMCW_Lesson_12_PicoW (saved by Fritzing 1.0.4)
circuit board: 6.19887cm x 5.6197cm
breadboards: 1

parts:
  Mod1 = Raspberry Pi Pico W
  LED2 = RGB LED (com. cathode, rgb) [color="Red (633nm)" current=0.030A package="5 mm [THT]"]
  R1 = Resistor [tolerance=±5% power=0.25W resistance=220 package=THT]
  R2 = Resistor [tolerance=±5% power=0.25W resistance=220 package=THT]
  R4 = Resistor [tolerance=±5% power=0.25W resistance=220 package=THT]

nets:
  N1: Mod1.pin_3, Mod1.pin_8, Mod1.pin_13, Mod1.pin_18, Mod1.pin_23, Mod1.pin_28, Mod1.pin_33, Mod1.pin_38, LED2.common_cathode
  N2: Mod1.pin_21, R1.Pin_0
  N3: Mod1.pin_22, R4.Pin_0
  N4: Mod1.pin_24, R2.Pin_0
  N5: LED2.red_anode, R1.Pin_1
  N6: LED2.green_anode, R4.Pin_1
  N7: LED2.blue_anode, R2.Pin_1

custom parts:
  Raspberry Pi Pico W: Raspberry Pi Pico W. Based around the RP2040 microcontroller the Pico W is a low cost microcontroller device bringing Raspberry Pi quality, cost, and easy of use to the microcontroller space. The areas marked KEEPOUT in pcb silkscreen should not have traces running through them to avoid shorts on a soldered in module!
