# Fritzing sketch PMCW_Lesson_12_XTRACRDT (saved by Fritzing 1.0.4)
breadboards: 1

parts:
  Mod1 = Raspberry Pi Pico W
  R1 = Rotary Potentiometer (Small) [maximum_resistance=10kΩ knob_status=50% power=0.5W package=THT]
  R2 = Rotary Potentiometer (Small) [maximum_resistance=10kΩ knob_status=50% power=0.5W package=THT]
  R3 = Rotary Potentiometer (Small) [maximum_resistance=10kΩ knob_status=50% power=0.5W package=THT]
  LED1 = RGB LED (com. cathode, rgb) [color="Red (633nm)" current=0.030A package="5 mm [THT]"]
  R4 = Resistor [tolerance=±5% power=0.25W resistance=220 package=THT]
  R5 = Resistor [tolerance=±5% power=0.25W resistance=220 package=THT]
  R6 = Resistor [tolerance=±5% power=0.25W resistance=220 package=THT]

nets:
  N1: Mod1.pin_3, Mod1.pin_8, Mod1.pin_13, Mod1.pin_18, Mod1.pin_23, Mod1.pin_28, Mod1.pin_33, Mod1.pin_38, Mod1.pin_42, R1.leg1, R2.leg1, R3.leg1
  N2: Mod1.pin_17, R4.Pin_1
  N3: Mod1.pin_19, R5.Pin_1
  N4: Mod1.pin_20, R6.Pin_1
  N5: Mod1.pin_31, R3.wiper
  N6: Mod1.pin_32, R2.wiper
  N7: Mod1.pin_34, R1.wiper
  N8: R1.leg2, R2.leg2, R3.leg2
  N9: LED1.red_anode, R4.Pin_0
  N10: LED1.green_anode, R5.Pin_0
  N11: LED1.blue_anode, R6.Pin_0

custom parts:
  Raspberry Pi Pico W: Raspberry Pi Pico W. Based around the RP2040 microcontroller the Pico W is a low cost microcontroller device bringing Raspberry Pi quality, cost, and easy of use to the microcontroller space. The areas marked KEEPOUT in pcb silkscreen should not have traces running through them to avoid shorts on a soldered in module!
