# Fritzing sketch PMCW_Lesson_15_RGB_For_Loop (saved by Fritzing 1.0.4)
breadboards: 1

parts:
  Mod1 = Raspberry Pi Pico W
  LED1 = RGB LED (com. cathode, rgb) [color="Red (633nm)" current=0.030A package="5 mm [THT]"]
  R4 = Resistor [tolerance=±5% power=0.25W resistance=220 package=THT]
  R5 = Resistor [tolerance=±5% power=0.25W resistance=220 package=THT]
  R6 = Resistor [tolerance=±5% power=0.25W resistance=220 package=THT]

nets:
  N1: Mod1.pin_3, Mod1.pin_8, Mod1.pin_13, Mod1.pin_18, Mod1.pin_23, Mod1.pin_28, Mod1.pin_33, Mod1.pin_38, LED1.common_cathode
  N2: Mod1.pin_17, R4.Pin_1
  N3: Mod1.pin_19, R5.Pin_1
  N4: Mod1.pin_20, R6.Pin_1
  N5: LED1.red_anode, R4.Pin_0
  N6: LED1.green_anode, R5.Pin_0
  N7: LED1.blue_anode, R6.Pin_0

custom parts:
  Raspberry Pi Pico W: Raspberry Pi Pico W. Based around the RP2040 microcontroller the Pico W is a low cost microcontroller device bringing Raspberry Pi quality, cost, and easy of use to the microcontroller space. The areas marked KEEPOUT in pcb silkscreen should not have traces running through them to avoid shorts on a soldered in module!
