# Fritzing sketch PMCW Lesson 18 Home work Schematic (saved by Fritzing 1.0.4)
circuit board: 8.50131cm x 5.75527cm
breadboards: 1

parts:
  Mod1 = Raspberry Pi Pico W
  Red_Button = Pushbutton [package="[THT]"]
  R1_220_ohm = Resistor [tolerance=±5% power=0.25W resistance=220 package=THT]
  RGB_LED = RGB LED (com. cathode, rgb) [color="Red (633nm)" current=0.030A package="5 mm [THT]"]
  Green_Button = Pushbutton [package="[THT]"]
  Blue_Button = Pushbutton [package="[THT]"]

nets:
  N1: Mod1.pin_3, Mod1.pin_8, Mod1.pin_13, Mod1.pin_18, Mod1.pin_23, Mod1.pin_28, Mod1.pin_33, Mod1.pin_38, Red_Button.Pin_1, Red_Button.Pin_2, R1_220_ohm.Pin_0, Green_Button.Pin_1, Green_Button.Pin_2, Blue_Button.Pin_1, Blue_Button.Pin_2
  N2: Mod1.pin_17, RGB_LED.red_anode
  N3: Mod1.pin_19, RGB_LED.green_anode
  N4: Mod1.pin_20, RGB_LED.blue_anode
  N5: Mod1.pin_21, Red_Button.Pin_3, Red_Button.Pin_4
  N6: Mod1.pin_22, Green_Button.Pin_3, Green_Button.Pin_4
  N7: Mod1.pin_24, Blue_Button.Pin_3, Blue_Button.Pin_4
  N8: R1_220_ohm.Pin_1, RGB_LED.common_cathode

custom parts:
  Raspberry Pi Pico W: Raspberry Pi Pico W. Based around the RP2040 microcontroller the Pico W is a low cost microcontroller device bringing Raspberry Pi quality, cost, and easy of use to the microcontroller space. The areas marked KEEPOUT in pcb silkscreen should not have traces running through them to avoid shorts on a soldered in module!
